// Logisim project classic.circ as structural Verilog: 2 circuits, main circuit Demo
module AND2 (
  input  A,
  input  B,
  output Y
);

  // AND_Gate and_1: pin names not known; wires that end beside it: A, B, Y
endmodule

module Demo (
  input  In,
  output Out
);

  // AND2 and2_1: pin names not known; wires that end beside it: In, Out
endmodule
