// Logisim project main.circ as structural Verilog: 5 circuits, main circuit ALU
module Half_Adder (
  input  A,
  input  B,
  output Sum,
  output Carry
);

  // XOR_Gate xor_1 has open pins: out=Sum
  // AND_Gate and_1 has open pins: out=Carry
endmodule

module Full_Adder (
  input  A,
  input  B,
  input  Cin,
  output Sum,
  output Cout
);

  // Half_Adder half_adder_1: pin names not known; wires that end beside it: A, B
  // Half_Adder half_adder_2: pin names not known; wires that end beside it: Sum, Cin
  // OR_Gate or_1 has open pins: out=Cout
endmodule

module Full_Adder_32_bit (
  input  [31:0] A,
  input  [31:0] B,
  input  Cin,
  output [31:0] Sum,
  output Cout
);

  // Full_Adder full_adder_1: pin names not known; wires that end beside it: A, B
  Full_Adder full_adder_2 ();  // open: A, B, Cin, Sum, Cout
  // Full_Adder full_adder_3: pin names not known; wires that end beside it: Sum
  Full_Adder full_adder_4 (.Sum(Cout));  // open: A, B, Cin, Cout
endmodule

module Multiplier_4_bit (
  input  [3:0] X,
  input  [3:0] Y,
  output [7:0] P
);

  // AND_Gate #(.width(4)) and_1: pin names not known; wires that end beside it: X, Y, P
endmodule

module ALU (
  input  [31:0] A,
  input  [31:0] B,
  input  [2:0] Op,
  output [31:0] Result
);

  // Full_Adder_32_bit full_adder_32_bit_1: pin names not known; wires that end beside it: A, Result, B
  Multiplier_4_bit multiplier_4_bit_1 ();  // open: X, Y, P
endmodule
